// Logisim project FullCirc.circ as structural Verilog: 6 circuits, main circuit RegisterFile
module RegisterFile (
  input  [3:0] RY,
  input  [3:0] RZ,
  input  [31:0] BusX,
  input  [3:0] RX,
  input  regWrite,
  input  CLK,
  output [31:0] BusY,
  output [31:0] BusZ
);

  wire and_1_out, and_2_out, and_3_out, and_4_out, and_5_out, and_6_out, and_7_out, and_8_out, and_9_out,
       and_10_out, and_11_out, and_12_out, and_13_out, and_14_out, and_15_out, decoder_1_out0,
       decoder_2_out0, decoder_2_out1, decoder_2_out2, decoder_2_out3, decoder_2_out4, decoder_2_out5,
       decoder_2_out6, decoder_2_out7, decoder_2_out8, decoder_2_out9, decoder_2_out10, decoder_2_out11,
       decoder_2_out12, decoder_2_out13, decoder_2_out14, decoder_2_out15, decoder_3_out0, decoder_3_out1,
       decoder_3_out2, decoder_3_out3, decoder_3_out4, decoder_3_out5, decoder_3_out6, decoder_3_out7,
       decoder_3_out8, decoder_3_out9, decoder_3_out10, decoder_3_out11, decoder_3_out12, decoder_3_out13,
       decoder_3_out14, decoder_3_out15, r1, r2, r3, r4, r5, r6, r7, r8, r9, r10, r11, r12, r13, r14, r15;
  wire [31:0] R1_q, R2_q, R3_q, R4_q, R5_q, R6_q, R7_q, R8_q, R9_q, R10_q, R11_q, R12_q, R13_q, R14_q, R15_q;

  Decoder #(.select(4), .enable("false")) decoder_1 (
    .out0(decoder_1_out0), .out1(r1), .out2(r2), .out3(r3), .out4(r4), .out5(r5), .out6(r6), .out7(r7),
    .out8(r8), .out9(r9), .out10(r10), .out11(r11), .out12(r12), .out13(r13), .out14(r14), .out15(r15),
    .sel(RX));
  and and_1 (and_1_out, r1, regWrite);
  and and_2 (and_2_out, r3, regWrite);
  and and_3 (and_3_out, r5, regWrite);
  and and_4 (and_4_out, r7, regWrite);
  and and_5 (and_5_out, r9, regWrite);
  and and_6 (and_6_out, r11, regWrite);
  and and_7 (and_7_out, r13, regWrite);
  and and_8 (and_8_out, r15, regWrite);
  and and_9 (and_9_out, r2, regWrite);
  and and_10 (and_10_out, r4, regWrite);
  and and_11 (and_11_out, r6, regWrite);
  and and_12 (and_12_out, r8, regWrite);
  and and_13 (and_13_out, r10, regWrite);
  and and_14 (and_14_out, r12, regWrite);
  and and_15 (and_15_out, r14, regWrite);
  Register #(.width(32)) u_R1 (.D(BusX), .en(and_1_out), .Q(R1_q), .clk(CLK));  // open: clr
  Register #(.width(32)) u_R2 (.D(BusX), .en(and_9_out), .Q(R2_q), .clk(CLK));  // open: clr
  Register #(.width(32)) u_R3 (.D(BusX), .en(and_2_out), .Q(R3_q), .clk(CLK));  // open: clr
  Register #(.width(32)) u_R4 (.D(BusX), .en(and_10_out), .Q(R4_q), .clk(CLK));  // open: clr
  Register #(.width(32)) u_R5 (.D(BusX), .en(and_3_out), .Q(R5_q), .clk(CLK));  // open: clr
  Register #(.width(32)) u_R6 (.D(BusX), .en(and_11_out), .Q(R6_q), .clk(CLK));  // open: clr
  Register #(.width(32)) u_R7 (.D(BusX), .en(and_4_out), .Q(R7_q), .clk(CLK));  // open: clr
  Register #(.width(32)) u_R8 (.D(BusX), .en(and_12_out), .Q(R8_q), .clk(CLK));  // open: clr
  Register #(.width(32)) u_R9 (.D(BusX), .en(and_5_out), .Q(R9_q), .clk(CLK));  // open: clr
  Register #(.width(32)) u_R10 (.D(BusX), .en(and_13_out), .Q(R10_q), .clk(CLK));  // open: clr
  Register #(.width(32)) u_R11 (.D(BusX), .en(and_6_out), .Q(R11_q), .clk(CLK));  // open: clr
  Register #(.width(32)) u_R12 (.D(BusX), .en(and_14_out), .Q(R12_q), .clk(CLK));  // open: clr
  Register #(.width(32)) u_R13 (.D(BusX), .en(and_7_out), .Q(R13_q), .clk(CLK));  // open: clr
  Register #(.width(32)) u_R14 (.D(BusX), .en(and_15_out), .Q(R14_q), .clk(CLK));  // open: clr
  Register #(.width(32)) u_R15 (.D(BusX), .en(and_8_out), .Q(R15_q), .clk(CLK));  // open: clr
  assign BusY = decoder_2_out0 ? {32{1'b0}} : 32'bz;  // Controlled_Buffer controlled_buffer_1
  assign BusY = decoder_2_out1 ? R1_q : 32'bz;  // Controlled_Buffer controlled_buffer_2
  assign BusY = decoder_2_out2 ? R2_q : 32'bz;  // Controlled_Buffer controlled_buffer_3
  assign BusY = decoder_2_out3 ? R3_q : 32'bz;  // Controlled_Buffer controlled_buffer_4
  assign BusY = decoder_2_out4 ? R4_q : 32'bz;  // Controlled_Buffer controlled_buffer_5
  assign BusY = decoder_2_out5 ? R5_q : 32'bz;  // Controlled_Buffer controlled_buffer_6
  assign BusY = decoder_2_out6 ? R6_q : 32'bz;  // Controlled_Buffer controlled_buffer_7
  assign BusY = decoder_2_out7 ? R7_q : 32'bz;  // Controlled_Buffer controlled_buffer_8
  assign BusY = decoder_2_out8 ? R8_q : 32'bz;  // Controlled_Buffer controlled_buffer_9
  assign BusY = decoder_2_out9 ? R9_q : 32'bz;  // Controlled_Buffer controlled_buffer_10
  assign BusY = decoder_2_out10 ? R10_q : 32'bz;  // Controlled_Buffer controlled_buffer_11
  assign BusY = decoder_2_out11 ? R11_q : 32'bz;  // Controlled_Buffer controlled_buffer_12
  assign BusY = decoder_2_out12 ? R12_q : 32'bz;  // Controlled_Buffer controlled_buffer_13
  assign BusY = decoder_2_out13 ? R13_q : 32'bz;  // Controlled_Buffer controlled_buffer_14
  assign BusY = decoder_2_out14 ? R14_q : 32'bz;  // Controlled_Buffer controlled_buffer_15
  assign BusY = decoder_2_out15 ? R15_q : 32'bz;  // Controlled_Buffer controlled_buffer_16
  Decoder #(.select(4), .enable("false")) decoder_2 (
    .out0(decoder_2_out0), .out1(decoder_2_out1), .out2(decoder_2_out2), .out3(decoder_2_out3),
    .out4(decoder_2_out4), .out5(decoder_2_out5), .out6(decoder_2_out6), .out7(decoder_2_out7),
    .out8(decoder_2_out8), .out9(decoder_2_out9), .out10(decoder_2_out10), .out11(decoder_2_out11),
    .out12(decoder_2_out12), .out13(decoder_2_out13), .out14(decoder_2_out14), .out15(decoder_2_out15),
    .sel(RY));
  assign BusZ = decoder_3_out0 ? {32{1'b0}} : 32'bz;  // Controlled_Buffer controlled_buffer_17
  assign BusZ = decoder_3_out1 ? R1_q : 32'bz;  // Controlled_Buffer controlled_buffer_18
  assign BusZ = decoder_3_out2 ? R2_q : 32'bz;  // Controlled_Buffer controlled_buffer_19
  assign BusZ = decoder_3_out3 ? R3_q : 32'bz;  // Controlled_Buffer controlled_buffer_20
  assign BusZ = decoder_3_out4 ? R4_q : 32'bz;  // Controlled_Buffer controlled_buffer_21
  assign BusZ = decoder_3_out5 ? R5_q : 32'bz;  // Controlled_Buffer controlled_buffer_22
  assign BusZ = decoder_3_out6 ? R6_q : 32'bz;  // Controlled_Buffer controlled_buffer_23
  assign BusZ = decoder_3_out7 ? R7_q : 32'bz;  // Controlled_Buffer controlled_buffer_24
  assign BusZ = decoder_3_out8 ? R8_q : 32'bz;  // Controlled_Buffer controlled_buffer_25
  assign BusZ = decoder_3_out9 ? R9_q : 32'bz;  // Controlled_Buffer controlled_buffer_26
  assign BusZ = decoder_3_out10 ? R10_q : 32'bz;  // Controlled_Buffer controlled_buffer_27
  assign BusZ = decoder_3_out11 ? R11_q : 32'bz;  // Controlled_Buffer controlled_buffer_28
  assign BusZ = decoder_3_out12 ? R12_q : 32'bz;  // Controlled_Buffer controlled_buffer_29
  assign BusZ = decoder_3_out13 ? R13_q : 32'bz;  // Controlled_Buffer controlled_buffer_30
  assign BusZ = decoder_3_out14 ? R14_q : 32'bz;  // Controlled_Buffer controlled_buffer_31
  assign BusZ = decoder_3_out15 ? R15_q : 32'bz;  // Controlled_Buffer controlled_buffer_32
  Decoder #(.select(4), .enable("false")) decoder_3 (
    .out0(decoder_3_out0), .out1(decoder_3_out1), .out2(decoder_3_out2), .out3(decoder_3_out3),
    .out4(decoder_3_out4), .out5(decoder_3_out5), .out6(decoder_3_out6), .out7(decoder_3_out7),
    .out8(decoder_3_out8), .out9(decoder_3_out9), .out10(decoder_3_out10), .out11(decoder_3_out11),
    .out12(decoder_3_out12), .out13(decoder_3_out13), .out14(decoder_3_out14), .out15(decoder_3_out15),
    .sel(RZ));
endmodule

module ALU (
  input  [31:0] A,
  input  [31:0] B,
  input  [3:0] ALUsel,
  output [31:0] ALUres
);

  wire comparator_1_eq, comparator_2_lt;
  wire [31:0] adder_1_out, adder_2_out, and_1_out, and_2_out, bit_extender_1_out, bit_extender_2_out,
       negator_1_out, not_1_out, or_1_out, shifter_1_out, shifter_2_out, shifter_3_out, shifter_4_out,
       xor_1_out;

  assign not_1_out = ~A;  // NOT_Gate not_1, 32 bits wide
  Negator #(.width(32)) negator_1 (.in(A), .out(negator_1_out));
  assign and_1_out = A & B;  // AND_Gate and_1, 32 bits wide
  assign and_2_out = not_1_out & B;  // AND_Gate and_2, 32 bits wide
  assign or_1_out = A | B;  // OR_Gate or_1, 32 bits wide
  assign xor_1_out = A ^ B;  // XOR_Gate xor_1, 32 bits wide
  Adder #(.width(32)) adder_1 (.a(A), .b(B), .out(adder_1_out));  // open: cin, cout
  Adder #(.width(32)) adder_2 (.a(negator_1_out), .b(B), .out(adder_2_out));  // open: cin, cout
  Comparator #(.width(32)) comparator_1 (.a(A), .b(B), .eq(comparator_1_eq));  // open: gt, lt
  Comparator #(.width(32)) comparator_2 (.a(A), .b(B), .lt(comparator_2_lt));  // open: gt, eq
  Shifter #(.width(32)) shifter_1 (.in(A), .\dist (B[4:0]), .out(shifter_1_out));
  Shifter #(.width(32), .shift("lr")) shifter_2 (.in(A), .\dist (B[4:0]), .out(shifter_2_out));
  Shifter #(.width(32), .shift("ar")) shifter_3 (.in(A), .\dist (B[4:0]), .out(shifter_3_out));
  Shifter #(.width(32), .shift("rr")) shifter_4 (.in(A), .\dist (B[4:0]), .out(shifter_4_out));
  assign bit_extender_1_out = {{31{1'b0}}, comparator_1_eq};  // Bit_Extender bit_extender_1
  assign bit_extender_2_out = {{31{1'b0}}, comparator_2_lt};  // Bit_Extender bit_extender_2
  Multiplexer #(.select(4), .width(32), .enable("false")) multiplexer_1 (
    .in0(and_1_out), .in1(and_2_out), .in2(or_1_out), .in3(xor_1_out), .in4(adder_1_out), .in5(adder_2_out),
    .in6(bit_extender_1_out), .in7(bit_extender_2_out), .in8(shifter_1_out), .in9(shifter_2_out),
    .in10(shifter_3_out), .in11(shifter_4_out), .out(ALUres), .sel(ALUsel));  // open: in12, in13, in14, in15

  // Notes on the sheet:
  //                                                  control  the shifting
  //   only the first four bits from the right of the bottom line
endmodule

// 12
module SCP (
  output [1:0] out_1,
  output out_2,
  output [3:0] out_3,
  output [1:0] out_4,
  output out_5,
  output [31:0] out_6,
  output [31:0] out_7,
  output [31:0] out_8,
  output [31:0] out_9,
  output [31:0] out_10
);

  wire CLK_out, MemRead, RegDst, RegWrite, undriven;
  wire [1:0] Wbdata;
  wire [3:0] multiplexer_2_out, multiplexer_3_out;
  wire [7:0] IMM8, OP, shifter_2_out;
  wire [15:0] shifter_1_out, shifter_3_out;
  wire [15:8] IMM16;
  wire [19:0] adder_1_out, adder_2_out, IMM8EXTENDED, IMM16EXTENDED, multiplexer_1_out, PC, PC_3;
  wire [31:0] alu_1_alures, bit_extender_5_out, IMM16EXTENDED32, multiplexer_4_out, ram_1_data;

  Adder #(.width(20)) adder_1 (.a(PC), .b(IMM8EXTENDED), .out(adder_1_out));  // open: cin, cout
  Adder #(.width(20)) adder_2 (.a(PC), .b(IMM16EXTENDED), .out(adder_2_out));  // open: cin, cout
  Shifter #(.width(16)) shifter_1 (.in({IMM16, IMM8}), .\dist (4'b0001), .out(shifter_1_out));
  RxSel rxsel_1 (.OpCode(OP), .sel(out_5));
  assign IMM16EXTENDED = {{4{shifter_1_out[15]}}, shifter_1_out};  // Bit_Extender bit_extender_1
  Multiplexer #(.select(2), .width(20), .enable("false")) multiplexer_1 (
    .in0(PC_3), .in1(adder_1_out), .in2(adder_2_out), .out(multiplexer_1_out), .sel(out_1));  // open: in3
  Register #(.width(20)) u_PC (.D(multiplexer_1_out), .en(1'b1), .Q(PC), .clk(CLK_out));  // open: clr
  Clock CLK (.out(CLK_out));
  Adder #(.width(20)) adder_3 (.a(PC), .b(20'h3), .out(PC_3));  // open: cin, cout
  ROM #(.addrWidth(20), .dataWidth(24)) rom_1 (.addr(PC), .data({OP, IMM16, IMM8}));  // open: sel
  assign out_8 = {{24{IMM8[7]}}, IMM8};  // Bit_Extender bit_extender_2
  Shifter shifter_2 (.in(IMM8), .\dist (3'b001), .out(shifter_2_out));
  Multiplexer #(.width(4), .enable("false")) multiplexer_2 (
    .in0(IMM16[15:12]), .in1(4'b1111), .out(multiplexer_2_out), .sel(RegDst));
  assign IMM8EXTENDED = {{12{shifter_2_out[7]}}, shifter_2_out};  // Bit_Extender bit_extender_3
  Multiplexer #(.width(4)) multiplexer_3 (
    .in0(IMM8[7:4]), .in1(IMM16[15:12]), .out(multiplexer_3_out), .sel(out_5), .en(undriven));
  RegisterFile registerfile_1 (
    .RX(multiplexer_2_out), .regWrite(RegWrite), .BusX(out_7), .RY(IMM16[11:8]), .BusY(out_6),
    .RZ(multiplexer_3_out), .BusZ(out_9), .CLK(CLK_out));
  ControlUnit controlunit_1 (
    .OPCODE(OP), .RegDest(RegDst), .RegWrite(RegWrite), .BSel(out_4), .memWrite(out_2), .memRead(MemRead),
    .Wbdata(Wbdata), .ALUsel(out_3));
  Multiplexer #(.select(2), .width(32), .enable("false")) multiplexer_4 (
    .in0(out_9), .in1(out_8), .in2(IMM16EXTENDED32), .out(multiplexer_4_out), .sel(out_4));  // open: in3
  pcCTR pcctr_1 (.BusX(out_9), .BusY(out_6), .OpCode(OP), .out_4(out_1));
  Shifter #(.width(16)) shifter_3 (.in({IMM16, IMM8}), .\dist (4'b1111), .out(shifter_3_out));
  ALU alu_1 (.A(out_6), .B(multiplexer_4_out), .ALUsel(out_3), .ALUres(alu_1_alures));
  assign IMM16EXTENDED32 = {{16{shifter_3_out[15]}}, shifter_3_out};  // Bit_Extender bit_extender_4
  RAM #(.addrWidth(20), .dataWidth(32), .bus("separate")) ram_1 (
    .addr(alu_1_alures[19:0]), .din(out_9), .data(ram_1_data), .str(out_2), .clk(CLK_out), .ld(MemRead));  // open: sel, clr
  assign bit_extender_5_out = {{12{PC_3[19]}}, PC_3};  // Bit_Extender bit_extender_5
  Multiplexer #(.select(2), .width(32), .enable("false")) multiplexer_5 (
    .in0(alu_1_alures), .in1(ram_1_data), .in2(bit_extender_5_out), .in3({32{1'b0}}), .out(out_7),
    .sel(Wbdata));

  assign out_10 = out_7;

  // Other names for the same wires on the sheet: IMM16[7:0] = IMM8; Z[3:0] = IMM8[7:4]; Y[3:0] = IMM16[11:8];
  //   X[3:0] = IMM16[15:12]; OPCODE[7:0] = OP; ALUop[3:0] = out_3; BSel[1:0] = out_4; MemWrite = out_2;
  //   pcCTR[1:0] = out_1; Sel = out_5

  // Notes on the sheet:
  //   contents of rom_1 (hex, n*v repeats v):
  //   a1005 0 0 a200a 0 0 3120 0 0 24120 0 0 45120 0 0 66110 0 0 77120 0 0 c8103 0 0 f9107 0 0 10a101 0 0
  //   13b202 0 0 116230 0 0 58320 0 0 141202 0 0 cd163 0 0 141102 0 0 0 97255 0 0 c0e930 0 0 1a0002 0 0 0
  //   161204 7*0 8d0f0 0 0 1b0002 0 0 0 35120 0 0 191004 0 0 186004 0 0 154502 0 0 c7007 0 0 151302 0 0 0
  //   b710f 0 0 171302
endmodule

module ControlUnit (
  input  [7:0] OPCODE,
  output RegDest,
  output RegWrite,
  output [1:0] BSel,
  output memWrite,
  output memRead,
  output [1:0] Wbdata,
  output [3:0] ALUsel
);

  ROM rom_1 (.addr(OPCODE), .data({RegDest, RegWrite, BSel, memWrite, memRead, Wbdata}));  // open: sel
  ROM #(.dataWidth(4)) rom_2 (.addr(OPCODE), .data(ALUsel));  // open: sel

  // Notes on the sheet:
  //   contents of rom_1 (hex, n*v repeats v):
  //   8*40 12*50 4*0 55 18 0 c2
  //   contents of rom_2 (hex, n*v repeats v):
  //   0 1 2 3 4 5 6 7 0 1 2 3 4 5 6 7 8 9 a b 4*0 4 4
endmodule

module pcCTR (
  input  [31:0] BusX,
  input  [31:0] BusY,
  input  [7:0] OpCode,
  output [1:0] out_4
);

  wire and_1_out, and_2_out, and_3_out, and_4_out, comparator_1_gt, decoder_1_out20, decoder_1_out21,
       decoder_1_out22, decoder_1_out23, decoder_1_out26, decoder_1_out27, EQ, GE, LT, NE, or_1_out, or_2_out;

  Decoder #(.select(5)) decoder_1 (
    .out20(decoder_1_out20), .out21(decoder_1_out21), .out22(decoder_1_out22), .out23(decoder_1_out23),
    .out26(decoder_1_out26), .out27(decoder_1_out27), .sel(OpCode[4:0]));  // open: out0, out1, out2, out3, out4, out5, out6, out7, out8, out9, out10, out11, out12, out13, out14, out15, out16, out17, out18, out19, out24, out25, out28, out29, out30, out31, en
  and and_1 (and_1_out, decoder_1_out20, EQ);
  and and_2 (and_2_out, decoder_1_out21, NE);
  and and_3 (and_3_out, decoder_1_out22, LT);
  and and_4 (and_4_out, decoder_1_out23, GE);
  or or_1 (or_1_out, and_1_out, and_2_out, and_3_out, and_4_out);
  or or_2 (or_2_out, decoder_1_out26, decoder_1_out27);
  Priority_Encoder #(.select(2)) priority_encoder_1 (
    .in0(1'b1), .in1(or_1_out), .in2(or_2_out), .in3(1'b0), .out(out_4));  // open: gs, en_out, en_in
  Comparator #(.width(32)) comparator_1 (.a(BusX), .b(BusY), .gt(comparator_1_gt), .eq(EQ), .lt(LT));
  or or_3 (GE, comparator_1_gt, EQ);
  or or_4 (NE, comparator_1_gt, LT);
endmodule

module RxSel (
  input  [7:0] OpCode,
  output sel
);

  wire decoder_1_out20, decoder_1_out21, decoder_1_out22, decoder_1_out23, decoder_1_out25, or_1_out;

  Decoder #(.select(5)) decoder_1 (
    .out20(decoder_1_out20), .out21(decoder_1_out21), .out22(decoder_1_out22), .out23(decoder_1_out23),
    .out25(decoder_1_out25), .sel(OpCode[4:0]));  // open: out0, out1, out2, out3, out4, out5, out6, out7, out8, out9, out10, out11, out12, out13, out14, out15, out16, out17, out18, out19, out24, out26, out27, out28, out29, out30, out31, en
  or or_1 (or_1_out, decoder_1_out20, decoder_1_out21, decoder_1_out22, decoder_1_out23, decoder_1_out25);
  Priority_Encoder #(.select(1)) priority_encoder_1 (.in0(1'b1), .in1(or_1_out), .out(sel));  // open: gs, en_out, en_in
endmodule
